// Digital circuit processor.dig as structural Verilog
module processor (
  input  reset,
  input  en_write,
  input  start,
  input  data_in,
  input  clk,
  output states
);

  wire ACC_OPX, ACC_OPY, add_1_s, alu_1_p6, BRANCH, comparator_1_eq, dm_1_p1, DONE, JMP, LOAD_A, LOAD_B,
       LOAD_X, LOAD_Y, MOVE, multiplexer_1_out, multiplexer_2_out, multiplexer_3_out, multiplexer_4_out,
       multiplexer_5_out, multiplexer_6_out, or_1_out, pc_1_p7, POP, PUSH, reg_file_1_p4, reg_file_1_p5,
       reg_file_1_p6, reg_file_1_p9, reg_file_1_p10, reg_file_1_p11, reg_file_1_p14, RESET_CU, RET, STALL,
       STORE, STORE_TENSOR, STR_REZ, STR_TENSOR_REZ;
  wire [3:0] counter_1_p4;
  wire [7:0] pc_1_p5;
  wire [8:0] reg_file_1_p8, reg_file_1_p12;
  wire [15:0] bitextender_1_out, bitextender_2_out;
  wire [15:9] reg_file_1_p8_2;

  Multiplexer multiplexer_1 (.sel(RET), .in_0(reg_file_1_p8[0]), .out(multiplexer_1_out));  // open: in_1
  // PC pc_1: pin names not known; wires that end beside it: reset, BRANCH, STALL, multiplexer_1_out, pc_1_p5, clk, pc_1_p7
  // incrementer incrementer_1: pin names not known; wires that end beside it: pc_1_p7, pc_1_p5
  IM im_1 (.clk(en_write), .en_write(pc_1_p7), .address(data_in), .data_in(clk));  // open: data_out
  // counter counter_1: pin names not known; wires that end beside it: reset, STALL, clk, counter_1_p4
  // reg_file reg_file_1: pin names not known; wires that end beside it: reset, {DONE, RESET_CU, STR_TENSOR_REZ, STORE_TENSOR, LOAD_B, LOAD_A, RET, JMP, ACC_OPY, ACC_OPX, LOAD_X, LOAD_Y, STR_REZ, STALL, PUSH, POP, BRANCH, STORE, MOVE}, counter_1_p4, reg_file_1_p4, reg_file_1_p5, reg_file_1_p6, clk, {reg_file_1_p8_2, reg_file_1_p8}, reg_file_1_p9, reg_file_1_p10, reg_file_1_p11, reg_file_1_p12, reg_file_1_p8_2[15:10], reg_file_1_p14
  Multiplexer multiplexer_2 (
    .sel(reg_file_1_p8_2[9]), .in_0(reg_file_1_p9), .in_1(reg_file_1_p10), .out(multiplexer_2_out));
  Add add_1 (.a(reg_file_1_p8[0]), .b(counter_1_p4[0]), .c_i(1'b0), .s(add_1_s));  // open: c_o
  Comparator comparator_1 (.a(counter_1_p4[0]), .b(1'b1), .eq(comparator_1_eq));  // open: gt, lt
  BitExtender bitextender_1 (.in(reg_file_1_p8[7:0]), .out(bitextender_1_out));
  // MXU mxu_1: pin names not known; wires that end beside it: reg_file_1_p8_2[15:10], reg_file_1_p14, reg_file_1_p4
  // alu alu_1: pin names not known; wires that end beside it: STORE, multiplexer_2_out, bitextender_1_out, reg_file_1_p8_2[15:10], reg_file_1_p5, alu_1_p6
  Multiplexer multiplexer_3 (.sel(or_1_out), .in_0(reg_file_1_p8[0]), .in_1(add_1_s), .out(multiplexer_3_out));
  or or_1 (or_1_out, LOAD_A, LOAD_B, STORE_TENSOR);
  BitExtender bitextender_2 (.in(pc_1_p5), .out(bitextender_2_out));
  Multiplexer #(.Selector_Bits(4)) multiplexer_4 (
    .sel(counter_1_p4), .in_0(reg_file_1_p12[0]), .in_1(reg_file_1_p12[1]), .in_2(reg_file_1_p12[2]),
    .in_3(reg_file_1_p12[3]), .in_4(reg_file_1_p12[4]), .in_5(reg_file_1_p12[5]), .in_6(reg_file_1_p12[6]),
    .in_7(reg_file_1_p12[7]), .in_8(reg_file_1_p12[8]), .in_9(1'b0), .in_10(1'b0), .in_11(1'b0),
    .in_12(1'b0), .in_13(1'b0), .in_14(1'b0), .in_15(1'b0), .out(multiplexer_4_out));
  // control_unit control_unit_1: pin names not known; wires that end beside it: reset, start, comparator_1_eq, reg_file_1_p8[8], reg_file_1_p8_2[9], reg_file_1_p8_2[15:10], alu_1_p6, clk, {DONE, RESET_CU, STR_TENSOR_REZ, STORE_TENSOR, LOAD_B, LOAD_A, RET, JMP, ACC_OPY, ACC_OPX, LOAD_X, LOAD_Y, STR_REZ, STALL, PUSH, POP, BRANCH, STORE, MOVE}, states
  Multiplexer multiplexer_5 (.sel(JMP), .in_0(reg_file_1_p5), .in_1(bitextender_2_out[0]), .out(multiplexer_5_out));
  Multiplexer multiplexer_6 (
    .sel(STORE_TENSOR), .in_0(multiplexer_5_out), .in_1(multiplexer_4_out), .out(multiplexer_6_out));
  // DM dm_1: pin names not known; wires that end beside it: dm_1_p1, PUSH, POP, multiplexer_6_out, reg_file_1_p11, multiplexer_3_out, clk, reg_file_1_p6
  or or_2 (dm_1_p1, STORE, STORE_TENSOR);
  // Pins of 1 and 10 bits meet at {reg_file_1_p8_2[9], reg_file_1_p8}
  // Pins of 1 and 8 and 9 bits meet at reg_file_1_p8
  // Pins of 1 and 16 bits meet at bitextender_2_out
  // Pins of 1 and 4 bits meet at counter_1_p4
  // Pins of 1 and 3 bits meet at 3'b000
  // Pins of 1 and 4 bits meet at 4'b1001
endmodule
