// Digital circuit reg_file.dig as structural Verilog
module reg_file (
  input  reset,
  input  [18:0] control_lines,
  input  counter_out,
  input  [63:0] mxu_out,
  input  alu_out,
  input  dm_out,
  input  clk,
  output acc_out,
  output x_out,
  output y_out,
  output sp_out,
  output [63:0] t_acc_out,
  output a_out,
  output b_out
);

  wire inc_dec_sp_1_val, undriven;

  tensor_register A (
    .reset(reset), .element(dm_out), .load(control_lines[13]), .idx(counter_out), .clk(clk),
    .tensor_out(a_out));
  tensor_register B (
    .reset(reset), .element(dm_out), .load(control_lines[14]), .idx(counter_out), .clk(clk),
    .tensor_out(b_out));
  accumulator accumulator_1 (.reset(reset), .str_rez(control_lines[6]), .alu_out(undriven), .clk(clk), .out(acc_out));
  register reg_x (
    .reset(reset), .acc_op(control_lines[9]), .load(control_lines[8]), .acc_val(acc_out), .data_val(dm_out),
    .clk(clk), .out(x_out));
  register reg_y (
    .reset(reset), .acc_op(control_lines[10]), .load(control_lines[7]), .acc_val(acc_out), .data_val(dm_out),
    .clk(clk), .out(y_out));
  SP stack_pointer (
    .reset(reset), .pop(control_lines[3]), .push(control_lines[4]), .new_sp_val(inc_dec_sp_1_val), .clk(clk),
    .out(sp_out));
  INC_DEC_SP inc_dec_sp_1 (.pop(control_lines[3]), .sp(sp_out), .val(inc_dec_sp_1_val));
  tensor_accumulator tensor_accumulator_1 (
    .reset(reset), .str_rez(control_lines[16]), .mxu_out(mxu_out), .clk(clk), .acc_out(t_acc_out));
  // Pins of 1 and 19 bits meet at control_lines
  // Pins of 1 and 64 bits meet at mxu_out
  // Pins of 1 and 64 bits meet at t_acc_out
endmodule
