// Digital circuit Processor.dig as structural Verilog
module Processor (
);

  wire acc_op, acc_opx, acc_opy, accumulator_1_val, alu_1_p5, alu_1_p8, alu_1_p9, branch, control_unit_1_p3,
       control_unit_1_p4, control_unit_1_p5, dm_1_p7, done, inc_dec_sp_1_val, load, load_x, load_y, pc_1_p4,
       pc_1_p5, pop, push, \reg , reg_s, reg_x_1_x, reg_y_1_y, sign_extend_1_p2, sp_1_out, stall, store,
       str_rez, undriven, undriven_2;
  wire [1:0] pc_1_p3;
  wire [5:0] ir_1_op_code;
  wire [7:0] pc_1_p3_2;
  wire [15:0] pc_1_p6;

  // PC pc_1: pin names not known; wires that end beside it: stall, branch, {pc_1_p3_2, pc_1_p3}, pc_1_p4, pc_1_p5, pc_1_p6
  IM im_1 (.en_write(undriven), .address(undriven_2), .data_in(pc_1_p5));  // open: clk, data_out
  // INC_PC inc_pc_1: pin names not known; wires that end beside it: pc_1_p5, pc_1_p4
  IR ir_1 (
    .instr_in(pc_1_p6), .op_code(ir_1_op_code), .acc_s(pc_1_p3[0]), .reg_s(pc_1_p3[1]), .value(pc_1_p3_2));  // open: clk
  // Sign_extend sign_extend_1: pin names not known; wires that end beside it: pc_1_p3_2, sign_extend_1_p2
  // Control_Unit control_unit_1: pin names not known; wires that end beside it: ir_1_op_code, pc_1_p3[0], control_unit_1_p3, control_unit_1_p4, control_unit_1_p5, store, branch, pop, push, stall, str_rez, acc_op, load_y, load_x, acc_opx, acc_opy, done
  // ALU alu_1: pin names not known; wires that end beside it: ir_1_op_code, sign_extend_1_p2, \reg , store, alu_1_p5, alu_1_p5, control_unit_1_p3, alu_1_p8, alu_1_p9
  SP sp_1 (.pop(pop), .push(push), .new_val(inc_dec_sp_1_val), .out(sp_1_out));  // open: reset, clk
  // DM dm_1: pin names not known; wires that end beside it: load, store, push, pop, {pc_1_p3_2, pc_1_p3[1]}, sp_1_out, dm_1_p7
  INC_DEC_SP inc_dec_sp_1 (.sp(sp_1_out), .pop(pop), .val(inc_dec_sp_1_val));
  // Flags flags_1: pin names not known; wires that end beside it: control_unit_1_p3, alu_1_p8, control_unit_1_p5
  accumulator accumulator_1 (.rez(alu_1_p9), .str_rez(str_rez), .val(accumulator_1_val));  // open: reset, clk
  Reg_Y reg_y_1 (
    .acc(accumulator_1_val), .load(load_y), .acc_op(acc_opy), .DM_val(dm_1_p7), .y(reg_y_1_y));  // open: reset, clk
  Reg_X reg_x_1 (
    .acc(accumulator_1_val), .load(load_x), .acc_op(acc_opx), .DM_val(dm_1_p7), .x(reg_x_1_x));  // open: reset, clk
  Multiplexer multiplexer_1 (.sel(reg_s), .in_0(reg_x_1_x), .in_1(reg_y_1_y), .out(\reg ));
endmodule
