// Digital circuit reg_file.dig as structural Verilog
module reg_file (
  input  stall,
  input  branch,
  input  reset,
  input  [15:0] instr_in,
  input  br_address,
  input  push,
  input  pop,
  input  ALU_ready,
  input  ALU_flags,
  input  rez,
  input  str_rez,
  input  acc_opx,
  input  acc_opy,
  input  load_x,
  input  load_y,
  input  DM_val,
  input  clk,
  output pc,
  output [5:0] op_code,
  output acc_s,
  output reg_s,
  output [7:0] imm,
  output SP,
  output flags,
  output acc,
  output x,
  output y,
  output \reg 
);

  wire inc_dec_sp_1_val, pc_1_p5;

  Flags flags_1 (.ALU_ready(ALU_ready), .ALU_flags(ALU_flags), .reset(reset), .clk(clk), .flags(flags));
  SP sp_1 (.reset(reset), .pop(pop), .push(push), .new_val(inc_dec_sp_1_val), .clk(clk), .out(SP));
  IR ir_1 (.instr_in(instr_in), .clk(clk), .op_code(op_code), .acc_s(acc_s), .reg_s(reg_s), .value(imm));
  // PC pc_1: pin names not known; wires that end beside it: stall, branch, reset, br_address, pc_1_p5, clk, pc
  INC_DEC_SP inc_dec_sp_1 (.sp(SP), .pop(pop), .val(inc_dec_sp_1_val));
  // INC_PC inc_pc_1: pin names not known; wires that end beside it: pc, pc_1_p5
  accumulator accumulator_1 (.rez(rez), .str_rez(str_rez), .reset(reset), .clk(clk), .val(acc));
  Reg_X reg_x_1 (.acc(acc), .reset(reset), .load(load_x), .acc_op(acc_opx), .DM_val(DM_val), .clk(clk), .x(x));
  Reg_Y reg_y_1 (.acc(acc), .reset(reset), .load(load_y), .acc_op(acc_opy), .DM_val(DM_val), .clk(clk), .y(y));
  Multiplexer multiplexer_1 (.sel(reg_s), .in_0(x), .in_1(y), .out(\reg ));
  // Pins of 1 and 16 bits meet at instr_in
  // Pins of 1 and 8 bits meet at imm
endmodule
